// Logisim project Lab02.circ as structural Verilog: 3 circuits, main circuit main
module main (
  input  X,
  input  Y,
  output out_3
);

  wire and_1_out, and_2_out, not_1_out, not_2_out;

  not not_1 (not_1_out, X);
  not not_2 (not_2_out, Y);
  and and_1 (and_1_out, not_1_out, Y);
  and and_2 (and_2_out, X, not_2_out);
  xor xor_1 (out_3, and_1_out, and_2_out);

  // Notes on the sheet:
  //   XOR Circuit
  //   Joshua Steffen 09/4/19
endmodule

module Full_Adder (
  input  X,
  input  Y,
  input  Carry_In,
  output Carry_out,
  output Sum
);

  wire half_adder_1_carry, half_adder_1_sum, half_adder_2_carry;

  Half_Adder half_adder_1 (.in_1(X), .in_2(Y), .Sum(half_adder_1_sum), .Carry(half_adder_1_carry));
  Half_Adder half_adder_2 (.in_1(Carry_In), .in_2(half_adder_1_sum), .Sum(Sum), .Carry(half_adder_2_carry));
  or or_1 (Carry_out, half_adder_1_carry, half_adder_2_carry);
endmodule

module Half_Adder (
  input  in_1,
  input  in_2,
  output Sum,
  output Carry
);

  wire and_1_out, and_2_out, not_1_out, not_2_out;

  not not_1 (not_1_out, in_1);
  and and_1 (and_1_out, not_1_out, not_1_out, in_2);
  and and_2 (and_2_out, in_1, not_2_out);
  not not_2 (not_2_out, in_2);
  and and_3 (Carry, in_1, in_2);
  xor xor_1 (Sum, and_1_out, and_2_out);
endmodule
